// Digital circuit fullAdder.dig as structural Verilog
module fullAdder (
  input  A,
  input  B,
  input  Cin,
  output Cout,
  output S
);

  wire halfadder_1_o_cout, halfadder_1_o_s, halfadder_2_o_cout;

  halfAdder halfadder_1 (.i_A(A), .i_B(B), .o_S(halfadder_1_o_s), .o_Cout(halfadder_1_o_cout));
  halfAdder halfadder_2 (.i_A(halfadder_1_o_s), .i_B(Cin), .o_S(S), .o_Cout(halfadder_2_o_cout));
  or or_1 (Cout, halfadder_1_o_cout, halfadder_2_o_cout);
endmodule
