// Digital circuit halfAdder.dig as structural Verilog
module halfAdder (
  input  i_A,
  input  i_B,
  output o_S,
  output o_Cout
);

  and and_1 (o_Cout, i_A, i_B);
  xor xor_1 (o_S, i_A, i_B);
endmodule
